# Fritzing sketch diagrama do placar (saved by Fritzing 0.9.3b)

parts:
  Componente1 = Arduino Mega 2560 (Rev3)
  U1 = 74HC595 [package="DIP16 [THT]"]
  U2 = 74HC595 [package="DIP16 [THT]"]
  U3 = 74HC595 [package="DIP16 [THT]"]
  U4 = 74HC595 [package="DIP16 [THT]"]
  U5 = 74HC595 [package="DIP16 [THT]"]
  U6 = 74HC595 [package="DIP16 [THT]"]
  U7 = 7-SEGMENT-DISPLAY [package=7-segment-display]
  U8 = 7-SEGMENT-DISPLAY [package=7-segment-display]
  U9 = 7-SEGMENT-DISPLAY [package=7-segment-display]
  U10 = 7-SEGMENT-DISPLAY [package=7-segment-display]
  U11 = 7-SEGMENT-DISPLAY [package=7-segment-display]
  U12 = 7-SEGMENT-DISPLAY [package=7-segment-display]
  S1 = SWITCH-MOMENTARY-2 [package=tactile-pth-12mm]
  S2 = SWITCH-MOMENTARY-2 [package=tactile-pth-12mm]
  S3 = SWITCH-MOMENTARY-2 [package=tactile-pth-12mm]
  S4 = SWITCH-MOMENTARY-2 [package=tactile-pth-12mm]
  S5 = SWITCH-MOMENTARY-2 [package=tactile-pth-12mm]
  S6 = SWITCH-MOMENTARY-2 [package=tactile-pth-12mm]
  S7 = SWITCH-MOMENTARY-2 [package=tactile-pth-12mm]
  S8 = SWITCH-MOMENTARY-2 [package=tactile-pth-12mm]
  S9 = SWITCH-MOMENTARY-2 [package=tactile-pth-12mm]
  U13 = 7-SEGMENT-4DIGIT [package=7-segment-4digit-youngsun]

nets:
  N1: Componente1.A8, U13.4
  N2: Componente1.A9, U13.3
  N3: Componente1.A10, U13.2
  N4: Componente1.A11, U13.1
  N5: Componente1.A0, U13.13
  N6: Componente1.A1, U13.14
  N7: Componente1.A2, U13.15
  N8: Componente1.A3, U13.16
  N9: Componente1.A4, U13.8
  N10: Componente1.A5, U13.7
  N11: Componente1.A6, U13.6
  N12: Componente1.A7, U13.5
  GND: Componente1.GND, U1.GND, U1.OE, U2.GND, U2.OE, U3.GND, U3.OE, U4.GND, U4.OE, U5.GND, U5.OE, U6.GND, U6.OE, U13.11
  N13: Componente1.D13_PWM, U4.SH_CP
  N14: Componente1.D12_PWM, U3.ST_CP, U4.ST_CP
  N15: Componente1.D11_PWM, U3.DS
  VCC: Componente1.5V, U1.MR, U1.VCC, U2.MR, U2.VCC, U3.MR, U3.VCC, U4.MR, U4.VCC, U5.MR, U5.VCC, U6.MR, U6.VCC, S1.2, S2.2, S3.2, S4.2, S5.2, S6.2, S7.2, S8.2, S9.2
  N16: Componente1.D0_RX0, U6.DS
  N17: Componente1.D1_TX0, U5.ST_CP
  N18: Componente1.D3_PWM, U5.SH_CP
  N19: Componente1.D5_PWM, U2.DS
  N20: Componente1.D6_PWM, U1.ST_CP
  N21: Componente1.D7_PWM, U1.SH_CP
  N22: Componente1.D45, S1.1
  N23: Componente1.D46, S2.1
  N24: Componente1.D47, S3.1
  N25: Componente1.D48, S4.1
  N26: Componente1.D49, S5.1
  N27: Componente1.D50, S6.1
  N28: Componente1.D51, S7.1
  N29: Componente1.D52, S8.1
  N30: Componente1.D53, S9.1
  N31: U1.Q1, U9.A
  N32: U1.Q2, U9.B
  N33: U1.Q3, U9.C
  N34: U1.Q4, U9.D
  N35: U1.Q5, U9.E
  N36: U1.Q6, U9.F
  N37: U1.Q7, U9.G
  N38: U1.DS, U2.Q7'
  N39: U2.Q1, U10.A
  N40: U2.Q2, U10.B
  N41: U2.Q3, U10.C
  N42: U2.Q4, U10.D
  N43: U2.Q5, U10.E
  N44: U2.Q6, U10.F
  N45: U2.Q7, U10.G
  N46: U3.Q1, U12.A
  N47: U3.Q2, U12.B
  N48: U3.Q3, U12.C
  N49: U3.Q4, U12.D
  N50: U3.Q5, U12.E
  N51: U3.Q6, U12.F
  N52: U3.Q7, U12.G
  N53: U3.Q7', U4.DS
  N54: U4.Q1, U11.A
  N55: U4.Q2, U11.B
  N56: U4.Q3, U11.C
  N57: U4.Q4, U11.D
  N58: U4.Q5, U11.E
  N59: U4.Q6, U11.F
  N60: U4.Q7, U11.G
  N61: U5.Q1, U7.A
  N62: U5.Q2, U7.B
  N63: U5.Q3, U7.C
  N64: U5.Q4, U7.D
  N65: U5.Q5, U7.E
  N66: U5.Q6, U7.F
  N67: U5.Q7, U7.G
  N68: U5.DS, U6.Q7'
  N69: U6.Q1, U8.A
  N70: U6.Q2, U8.B
  N71: U6.Q3, U8.C
  N72: U6.Q4, U8.D
  N73: U6.Q5, U8.E
  N74: U6.Q6, U8.F
  N75: U6.Q7, U8.G
  GND_2: U7.G2, U8.G2, U9.G2, U10.G2, U11.G2, U12.G2
