# Fritzing sketch diagrama elétrico atualizado do placar (saved by Fritzing 0.9.3b)

parts:
  Componente1 = Arduino Mega 2560 (Rev3)
  U1 = 74HC595 [package="DIP16 [THT]"]
  U2 = 74HC595 [package="DIP16 [THT]"]
  U3 = 74HC595 [package="DIP16 [THT]"]
  U4 = 74HC595 [package="DIP16 [THT]"]
  U5 = 74HC595 [package="DIP16 [THT]"]
  U6 = 74HC595 [package="DIP16 [THT]"]
  U7 = 7-SEGMENT-DISPLAY [package=7-segment-display]
  U8 = 7-SEGMENT-DISPLAY [package=7-segment-display]
  U9 = 7-SEGMENT-DISPLAY [package=7-segment-display]
  U10 = 7-SEGMENT-DISPLAY [package=7-segment-display]
  U11 = 7-SEGMENT-DISPLAY [package=7-segment-display]
  U12 = 7-SEGMENT-DISPLAY [package=7-segment-display]
  S1 = SWITCH-MOMENTARY-2 [package=tactile-pth-12mm]
  S2 = SWITCH-MOMENTARY-2 [package=tactile-pth-12mm]
  S3 = SWITCH-MOMENTARY-2 [package=tactile-pth-12mm]
  S4 = SWITCH-MOMENTARY-2 [package=tactile-pth-12mm]
  S5 = SWITCH-MOMENTARY-2 [package=tactile-pth-12mm]
  S6 = SWITCH-MOMENTARY-2 [package=tactile-pth-12mm]
  S7 = SWITCH-MOMENTARY-2 [package=tactile-pth-12mm]
  S8 = SWITCH-MOMENTARY-2 [package=tactile-pth-12mm]
  S9 = SWITCH-MOMENTARY-2 [package=tactile-pth-12mm]
  Display_4_dígitos = 4-Digit 7-segment LED Display [package=THT]

nets:
  N1: Componente1.A2, Display_4_dígitos.CLK
  N2: Componente1.A3, Display_4_dígitos.DIO
  GND: Componente1.GND, U1.GND, U1.OE, U2.GND, U2.OE, U3.GND, U3.OE, U4.GND, U4.OE, U5.GND, U5.OE, U6.GND, U6.OE, Display_4_dígitos.GND
  N3: Componente1.D13_PWM, U4.SH_CP
  N4: Componente1.D12_PWM, U3.ST_CP, U4.ST_CP
  N5: Componente1.D11_PWM, U3.DS
  VCC: Componente1.5V, U1.MR, U1.VCC, U2.MR, U2.VCC, U3.MR, U3.VCC, U4.MR, U4.VCC, U5.MR, U5.VCC, U6.MR, U6.VCC, S1.2, S2.2, S3.2, S4.2, S5.2, S6.2, S7.2, S8.2, S9.2, Display_4_dígitos.VCC
  N6: Componente1.D0_RX0, U6.DS
  N7: Componente1.D1_TX0, U5.ST_CP
  N8: Componente1.D3_PWM, U5.SH_CP
  N9: Componente1.D5_PWM, U2.DS
  N10: Componente1.D6_PWM, U1.ST_CP
  N11: Componente1.D7_PWM, U1.SH_CP
  N12: Componente1.D45, S1.1
  N13: Componente1.D46, S2.1
  N14: Componente1.D47, S3.1
  N15: Componente1.D48, S4.1
  N16: Componente1.D49, S5.1
  N17: Componente1.D50, S6.1
  N18: Componente1.D51, S7.1
  N19: Componente1.D52, S8.1
  N20: Componente1.D53, S9.1
  N21: U1.Q1, U9.A
  N22: U1.Q2, U9.B
  N23: U1.Q3, U9.C
  N24: U1.Q4, U9.D
  N25: U1.Q5, U9.E
  N26: U1.Q6, U9.F
  N27: U1.Q7, U9.G
  N28: U1.DS, U2.Q7'
  N29: U2.Q1, U10.A
  N30: U2.Q2, U10.B
  N31: U2.Q3, U10.C
  N32: U2.Q4, U10.D
  N33: U2.Q5, U10.E
  N34: U2.Q6, U10.F
  N35: U2.Q7, U10.G
  N36: U3.Q1, U12.A
  N37: U3.Q2, U12.B
  N38: U3.Q3, U12.C
  N39: U3.Q4, U12.D
  N40: U3.Q5, U12.E
  N41: U3.Q6, U12.F
  N42: U3.Q7, U12.G
  N43: U3.Q7', U4.DS
  N44: U4.Q1, U11.A
  N45: U4.Q2, U11.B
  N46: U4.Q3, U11.C
  N47: U4.Q4, U11.D
  N48: U4.Q5, U11.E
  N49: U4.Q6, U11.F
  N50: U4.Q7, U11.G
  N51: U5.Q1, U7.A
  N52: U5.Q2, U7.B
  N53: U5.Q3, U7.C
  N54: U5.Q4, U7.D
  N55: U5.Q5, U7.E
  N56: U5.Q6, U7.F
  N57: U5.Q7, U7.G
  N58: U5.DS, U6.Q7'
  N59: U6.Q1, U8.A
  N60: U6.Q2, U8.B
  N61: U6.Q3, U8.C
  N62: U6.Q4, U8.D
  N63: U6.Q5, U8.E
  N64: U6.Q6, U8.F
  N65: U6.Q7, U8.G
  GND_2: U7.G2, U8.G2, U9.G2, U10.G2, U11.G2, U12.G2

custom parts:
  4-Digit 7-segment LED Display: A 4-digit 7-segments LED display PCB module driven by a TM1637 control IC via 1-wire protocol.
